# Fritzing sketch Doohickey (saved by Fritzing 0.9.0b)

parts:
  Part1 = Arduino Mega 2560 (Rev3)
  Part2 = Arduino Wireless SD Shield
  LED2 = RGB LED (com. cathode, rgb) [package="5 mm [THT]"]
  R1 = Resistor [tolerance=±5% resistance=220 package=THT]
  S1 = Pushbutton [package=THT]
  LED3 = LED - 5mm [color="Red (633nm)" package="5 mm [THT]"]
  LED4 = LED - 5mm [color="Green (565nm)" package="5 mm [THT]"]
  T1 = LM35 Temperature Sensor [package="TO92 [THT]"]

nets:
  N1: Part1.A14, T1.Vout
  N2: Part1.A15, S1.leg0
  N3: Part1.D44, LED2.red_anode
  N4: Part1.D45, LED2.green_anode
  N5: Part1.D46, LED2.blue_anode
  N6: Part2.+5V, R1.Pin_0, S1.leg1
  N7: Part2.SD_CS, LED4.anode
  N8: Part2.D6, LED3.anode
  GND: Part2.GND, LED3.cathode, LED4.cathode, T1.GND
