# Fritzing sketch HVAC (saved by Fritzing 0.9.0b)
breadboards: 1

parts:
  LED1 = LED - 5mm [color="Red (633nm)" package="5 mm [THT]"]
  LED2 = LED - 5mm [color="Green (570nm)" package="5 mm [THT]"]
  T1 = LM35 Temperature Sensor [package="TO92 [THT]"]
  Part1 = Arduino Mega 2560 (Rev3)
  Part2 = Arduino Wireless SD Shield
  IC1 = IC, DIP package, 24 pins [chip_label=IC]
  VCC1 = 4 x AAA Battery Mount
  S1 = Toggle Switch [package=THT]

nets:
  GND: LED1.cathode, LED2.cathode, T1.GND, Part2.GND, IC1.pin7, VCC1.-, S1.L2
  N1: LED2.anode, Part2.SD_CS
  N2: T1.Vout, Part1.A14
  N3: Part1.A13, S1.COM
  N4: Part1.D32, IC1.pin8
  N5: Part1.D34, IC1.pin9
  N6: Part1.D36, IC1.pin10
  N7: Part2.+5V, IC1.pin12
  N8: Part2.VIN, VCC1.+

notes:
  To thermostat wires
